# Fritzing sketch steelsquid_PI_IO (saved by Fritzing 0.9.1b)
circuit board: 16cm x 10cm
breadboards: 1

parts:
  J27 = male pin header, 8 pins [form="♂ (male)"]
  J29 = double row male pin header, 20 pins [form="♂ (male)"]
  J33 = double row male pin header, 20 pins [form="♂ (male)"]
  J34 = double row male pin header, 20 pins [form="♂ (male)"]
  J35 = male pin header, 4 pins [form="♂ (male)"]
  UART40 = male pin header, 8 pins [form="♂ (male)"]
  UART41 = male pin header, 10 pins [form="♂ (male)"]
  UART43 = male pin header, 9 pins [form="♂ (male)"]
  J40 = male pin header, 4 pins [form="♂ (male)"]
  J39 = male pin header, 5 pins [form="♂ (male)"]
  J36 = male pin header, 6 pins [form="♂ (male)"]
  J44 = double row male pin header, 4 pins [form="♂ (male)"]
  J45 = double row male pin header, 4 pins [form="♂ (male)"]
  MCP23017 = IC, DIP package, 28 pins [chip_label=IC]
  UART53 = male pin header, 8 pins [form="♂ (male)"]
  UART54 = male pin header, 8 pins [form="♂ (male)"]
  J46 = double row male pin header, 18 pins [form="♂ (male)"]
  J47 = double row male pin header, 4 pins [form="♂ (male)"]
  J49 = male pin header, 2 pins [form="♂ (male)"]
  J28 = double row male pin header, 40 pins [form="♂ (male)"]
  J50 = male pin header, 2 pins [form="♂ (male)"]
  MCP23017_2 = IC, DIP package, 28 pins [chip_label=IC]
  UART55 = male pin header, 8 pins [form="♂ (male)"]
  UART56 = male pin header, 8 pins [form="♂ (male)"]
  MCP23017_3 = IC, DIP package, 28 pins [chip_label=IC]
  ULN2803A = IC, DIP package, 18 pins [chip_label=IC]
  UART60 = male pin header, 8 pins [form="♂ (male)"]
  ULN2803A_2 = IC, DIP package, 18 pins [chip_label=IC]
  UART62 = male pin header, 8 pins [form="♂ (male)"]
  DIP = IC, DIP package, 8 pins [chip_label=DIP]
  MCP23017_4 = IC, DIP package, 28 pins [chip_label=IC]
  LEFT = Momentary Switch [package=ksa_sealed_tac_switch]
  RIGHT = Momentary Switch [package=ksa_sealed_tac_switch]
  UP = Momentary Switch [package=ksa_sealed_tac_switch]
  DOWN = Momentary Switch [package=ksa_sealed_tac_switch]
  UART63 = male pin header, 4 pins [form="♂ (male)"]
  SELECT = Momentary Switch [package=ksa_sealed_tac_switch]
  J51 = male pin header, 1 pin [form="♂ (male)"]
  J52 = male pin header, 1 pin [form="♂ (male)"]
  ERROR = LED - 5mm [color="Red (633nm)" package="5 mm [THT]"]
  OK = LED - 5mm [color="Green (570nm)" package="5 mm [THT]"]
  J53 = male pin header, 3 pins [form="♂ (male)"]
  J54 = male pin header, 3 pins [form="♂ (male)"]
  J55 = male pin header, 2 pins [form="♂ (male)"]
  UART64 = male pin header, 4 pins [form="♂ (male)"]
  UART65 = male pin header, 5 pins [form="♂ (male)"]
  UART66 = male pin header, 5 pins [form="♂ (male)"]
  UART73 = male pin header, 6 pins [form="♂ (male)"]
  UART74 = male pin header, 4 pins [form="♂ (male)"]
  UART75 = male pin header, 4 pins [form="♂ (male)"]
  UART76 = male pin header, 6 pins [form="♂ (male)"]
  UART77 = male pin header, 4 pins [form="♂ (male)"]
  UART78 = male pin header, 4 pins [form="♂ (male)"]
  J57 = male pin header, 1 pin [form="♂ (male)"]
  J58 = male pin header, 1 pin [form="♂ (male)"]
  J59 = male pin header, 1 pin [form="♂ (male)"]
  J60 = male pin header, 2 pins [form="♂ (male)"]
  J63 = Screw terminal - 2 pins [package=THT]
  J48 = double row male pin header, 10 pins [form="♂ (male)"]
  Pad1 = Pad [width=5.19288888888889 height=7.2248888888889 connect=center]
  Pad2 = Pad [width=5.19288888888889 height=7.2248888888889 connect=center]  # not connected

nets:
  N1: J27.pin1, J28.pin8
  N2: J27.pin2, J28.pin9
  N3: J27.pin3, J28.pin31
  N4: J27.pin4, J28.pin30
  N5: J27.pin5, J28.pin32
  N6: J27.pin6, J27.pin7, UART43.pin9, MCP23017.pin9, MCP23017.pin18, J49.pin2, J28.pin29
  N7: J27.pin8, J29.pin1, J29.pin2, J29.pin3, J29.pin4, J29.pin5, J29.pin6, J29.pin7, J29.pin8, J29.pin9, J29.pin10, J29.pin11, J29.pin12, J29.pin13, J29.pin14, J29.pin15, J29.pin16, J29.pin17, J29.pin18, J29.pin19, J29.pin20, UART41.pin1, MCP23017.pin10, MCP23017.pin15, MCP23017.pin16, MCP23017.pin17, J49.pin1, J28.pin6, J28.pin40, J50.pin1, MCP23017_2.pin10, MCP23017_2.pin16, MCP23017_2.pin17, MCP23017_3.pin10, MCP23017_3.pin15, MCP23017_3.pin17, ULN2803A.pin9, ULN2803A_2.pin9, DIP.pin1, DIP.pin2, DIP.pin3, DIP.pin4, MCP23017_4.pin10, MCP23017_4.pin17, LEFT.3, RIGHT.3, RIGHT.4, UP.2, DOWN.4, SELECT.3, J52.pin1, ERROR.cathode, OK.cathode, UART65.pin5, UART73.pin5, UART76.pin2, UART76.pin5, J58.pin1, J60.pin1, J63.pin2, Pad1.pad
  N8: J33.pin1, J33.pin2, J33.pin3, J33.pin4, J33.pin5, J33.pin6, J33.pin7, J33.pin8, J33.pin9, J33.pin10, J33.pin11, J33.pin12, J33.pin13, J33.pin14, J33.pin15, J33.pin16, J33.pin17, J33.pin18, J33.pin19, J33.pin20, UART41.pin10, J28.pin19, J28.pin20, J50.pin2, MCP23017_2.pin9, MCP23017_2.pin15, MCP23017_2.pin18, MCP23017_3.pin9, MCP23017_3.pin16, MCP23017_3.pin18, MCP23017_4.pin9, MCP23017_4.pin15, MCP23017_4.pin16, MCP23017_4.pin18, UART66.pin5, UART73.pin2, UART73.pin6, UART76.pin6, J57.pin1
  N9: J34.pin1, J34.pin2, J34.pin3, J34.pin4, J34.pin5, J34.pin6, J34.pin7, J34.pin8, J34.pin9, J34.pin10, J34.pin11, J34.pin12, J34.pin13, J34.pin14, J34.pin15, J34.pin16, J34.pin17, J34.pin18, J34.pin19, J34.pin20, J28.pin21
  N10: J35.pin1, J28.pin5
  N11: J35.pin2, J28.pin3
  N12: J35.pin3, J28.pin2
  N13: J35.pin4, J28.pin1
  N14: UART40.pin1, UART41.pin2
  N15: UART40.pin2, UART41.pin3
  N16: UART40.pin3, UART41.pin4
  N17: UART40.pin4, UART41.pin5
  N18: UART40.pin5, UART41.pin6
  N19: UART40.pin6, UART41.pin7
  N20: UART40.pin7, UART41.pin8
  N21: UART40.pin8, UART41.pin9
  N22: UART43.pin1, J40.pin1, J28.pin24
  N23: UART43.pin2, J40.pin2, J28.pin26
  N24: UART43.pin3, J40.pin3, J28.pin27
  N25: UART43.pin4, J40.pin4, J28.pin28
  N26: UART43.pin5, J39.pin4, J28.pin38
  N27: UART43.pin6, J39.pin3, J28.pin37
  N28: UART43.pin7, J39.pin2, J28.pin36
  N29: UART43.pin8, J39.pin1, J28.pin35
  N30: J39.pin5, J28.pin39
  N31: J36.pin1, J28.pin17
  N32: J36.pin2, J28.pin16
  N33: J36.pin3, J28.pin15
  N34: J36.pin4, J28.pin13
  N35: J36.pin5, J28.pin12
  N36: J36.pin6, J28.pin10
  N37: J44.pin1, J44.pin2
  N38: J44.pin3, J44.pin4
  N39: J45.pin1, J45.pin2
  N40: J45.pin3, J45.pin4
  N41: MCP23017.pin1, UART53.pin8
  N42: MCP23017.pin2, UART53.pin7
  N43: MCP23017.pin3, UART53.pin6
  N44: MCP23017.pin4, UART53.pin5
  N45: MCP23017.pin5, UART53.pin4
  N46: MCP23017.pin6, UART53.pin3
  N47: MCP23017.pin7, UART53.pin2
  N48: MCP23017.pin8, UART53.pin1
  N49: MCP23017.pin12, J46.pin1, J46.pin2, J46.pin3, J46.pin4, J46.pin5, J46.pin6, J46.pin7, J46.pin8, J46.pin9, J47.pin1, J47.pin2, J28.pin23, MCP23017_2.pin12, MCP23017_3.pin12, MCP23017_4.pin12, UART66.pin4, UART73.pin4, UART76.pin4
  N50: MCP23017.pin13, J46.pin10, J46.pin11, J46.pin12, J46.pin13, J46.pin14, J46.pin15, J46.pin16, J46.pin17, J46.pin18, J47.pin3, J47.pin4, J28.pin22, MCP23017_2.pin13, MCP23017_3.pin13, MCP23017_4.pin13, UART66.pin3, UART73.pin3, UART76.pin3
  N51: MCP23017.pin21, UART54.pin1
  N52: MCP23017.pin22, UART54.pin2
  N53: MCP23017.pin23, UART54.pin3
  N54: MCP23017.pin24, UART54.pin4
  N55: MCP23017.pin25, UART54.pin5
  N56: MCP23017.pin26, UART54.pin6
  N57: MCP23017.pin27, UART54.pin7
  N58: MCP23017.pin28, UART54.pin8
  N59: MCP23017_2.pin1, UART55.pin8
  N60: MCP23017_2.pin2, UART55.pin7
  N61: MCP23017_2.pin3, UART55.pin6
  N62: MCP23017_2.pin4, UART55.pin5
  N63: MCP23017_2.pin5, UART55.pin4
  N64: MCP23017_2.pin6, UART55.pin3
  N65: MCP23017_2.pin7, UART55.pin2
  N66: MCP23017_2.pin8, UART55.pin1
  N67: MCP23017_2.pin21, UART56.pin1
  N68: MCP23017_2.pin22, UART56.pin2
  N69: MCP23017_2.pin23, UART56.pin3
  N70: MCP23017_2.pin24, UART56.pin4
  N71: MCP23017_2.pin25, UART56.pin5
  N72: MCP23017_2.pin26, UART56.pin6
  N73: MCP23017_2.pin27, UART56.pin7
  N74: MCP23017_2.pin28, UART56.pin8
  N75: MCP23017_3.pin1, ULN2803A.pin8
  N76: MCP23017_3.pin2, ULN2803A.pin7
  N77: MCP23017_3.pin3, ULN2803A.pin6
  N78: MCP23017_3.pin4, ULN2803A.pin5
  N79: MCP23017_3.pin5, ULN2803A.pin4
  N80: MCP23017_3.pin6, ULN2803A.pin3
  N81: MCP23017_3.pin7, ULN2803A.pin2
  N82: MCP23017_3.pin8, ULN2803A.pin1
  N83: MCP23017_3.pin21, ULN2803A_2.pin8
  N84: MCP23017_3.pin22, ULN2803A_2.pin7
  N85: MCP23017_3.pin23, ULN2803A_2.pin6
  N86: MCP23017_3.pin24, ULN2803A_2.pin5
  N87: MCP23017_3.pin25, ULN2803A_2.pin4
  N88: MCP23017_3.pin26, ULN2803A_2.pin3
  N89: MCP23017_3.pin27, ULN2803A_2.pin2
  N90: MCP23017_3.pin28, ULN2803A_2.pin1
  N91: ULN2803A.pin11, UART60.pin8
  N92: ULN2803A.pin12, UART60.pin7
  N93: ULN2803A.pin13, UART60.pin6
  N94: ULN2803A.pin14, UART60.pin5
  N95: ULN2803A.pin15, UART60.pin4
  N96: ULN2803A.pin16, UART60.pin3
  N97: ULN2803A.pin17, UART60.pin2
  N98: ULN2803A.pin18, UART60.pin1
  N99: ULN2803A_2.pin11, UART62.pin1
  N100: ULN2803A_2.pin12, UART62.pin2
  N101: ULN2803A_2.pin13, UART62.pin3
  N102: ULN2803A_2.pin14, UART62.pin4
  N103: ULN2803A_2.pin15, UART62.pin5
  N104: ULN2803A_2.pin16, UART62.pin6
  N105: ULN2803A_2.pin17, UART62.pin7
  N106: ULN2803A_2.pin18, UART62.pin8
  N107: DIP.pin5, MCP23017_4.pin6
  N108: DIP.pin6, MCP23017_4.pin7
  N109: DIP.pin7, MCP23017_4.pin5
  N110: DIP.pin8, MCP23017_4.pin4
  N111: MCP23017_4.pin1, UP.3
  N112: MCP23017_4.pin2, ERROR.anode
  N113: MCP23017_4.pin3, OK.anode
  N114: MCP23017_4.pin8, J51.pin1
  N115: MCP23017_4.pin21, UART63.pin4
  N116: MCP23017_4.pin22, UART63.pin3
  N117: MCP23017_4.pin23, UART63.pin2
  N118: MCP23017_4.pin24, UART63.pin1
  N119: MCP23017_4.pin25, DOWN.2
  N120: MCP23017_4.pin26, RIGHT.2
  N121: MCP23017_4.pin27, LEFT.2
  N122: MCP23017_4.pin28, SELECT.2
  N123: J53.pin1, J54.pin1
  N124: J53.pin2, J54.pin2
  N125: J53.pin3, J54.pin3
  N126: J55.pin1, J55.pin2, J48.pin1, J48.pin2, J48.pin3, J48.pin4, J48.pin5, J48.pin6, J48.pin7, J48.pin8, J48.pin9, J48.pin10
  N127: UART64.pin1, UART65.pin4
  N128: UART64.pin2, UART65.pin3
  N129: UART64.pin3, UART65.pin2
  N130: UART64.pin4, UART65.pin1
  N131: UART74.pin1, UART75.pin1
  N132: UART74.pin2, UART75.pin2
  N133: UART74.pin3, UART75.pin3
  N134: UART74.pin4, UART75.pin4
  N135: UART77.pin1, UART78.pin1
  N136: UART77.pin2, UART78.pin2
  N137: UART77.pin3, UART78.pin3
  N138: UART77.pin4, UART78.pin4
  N139: J59.pin1, J60.pin2, J63.pin1

notes:
  RST
  CE
  DC
  Din
  Clk
  VCC
  BL
  GND
  SCREWIN
  +V
  PSWITCH
  +5V
  ADJ
  +3V3
  TXB0108
  GPIO_PI_3V3
  GPIO_PI_5V
  I2C
  i2C
  SCL
  SDA
  TXD
  RXD
  5
  0
  1
  3
  4
  2
  7
  6
  A2 A1 A0
  TREX
  SERVO
  11/26
  12/19
  13/13
  14/06
  15/05
  1/21
  2/20
  3/16
  4/12
  5/25
  6/24
  7/23
  8/18
  9/15
  10/14
  16/22
  17/27
  18/17
  19/04
  17
  V1.0
  Steelsquid PIIO
  STEELSQUID.ORG
  GPIO_21_5V
  XGPIO5VA20
  GPIO_22_XV
  9
  13
  10
  15
  16
  14
  12
  11
  GPIO_23_5V
  RELAY
  SUM
  +ADJ
  UART
  GPIO_20_3V3
  8
  PIN/PI-GPIO
  UART_4
  DAC_61_5V
  Vo3
  Vo2
  Vo1
  Vo0
  MCP4728
  ADC_48_5V
  ADDR
  A2
  A3
  A0
  A1
  ADS1015
  ADC_49_5V
